// Logisim project carrylookaheadadder.circ as structural Verilog: 1 circuit, main circuit main
module main (
  input  [3:0] a,
  input  [3:0] in_2,
  input  c0,
  input  [3:0] b,
  output s0,
  output s1,
  output s2,
  output s3,
  output out_9
);

  wire and_1_out, and_2_out, and_3_out, and_4_out, and_5_out, and_6_out, and_7_out, and_8_out, and_9_out,
       and_10_out, and_11_out, and_12_out, and_13_out, and_14_out, c1_out, c2_out, c3_out, xor_1_out,
       xor_2_out, xor_3_out, xor_4_out;

  xor xor_1 (xor_1_out, a[3], b[3]);
  xor xor_2 (xor_2_out, a[2], b[2]);
  and and_1 (and_1_out, a[2], b[2]);
  and and_2 (and_2_out, a[3], b[3]);
  xor xor_3 (xor_3_out, a[0], b[0]);
  and and_3 (and_3_out, a[0], b[0]);
  xor xor_4 (xor_4_out, a[1], b[1]);
  buf and_4 (and_4_out, a[1]);  // AND_Gate
  and and_5 (and_5_out, c0, xor_3_out);
  and and_6 (and_6_out, and_5_out, xor_4_out);
  and and_7 (and_7_out, xor_4_out, and_3_out);
  and and_8 (and_8_out, and_4_out, xor_2_out);
  and and_9 (and_9_out, xor_4_out, and_3_out, xor_2_out);
  and and_10 (and_10_out, xor_4_out, xor_2_out, xor_3_out, c0);
  or c1 (c1_out, and_3_out, and_5_out);
  or c2 (c2_out, and_4_out, and_7_out, and_6_out);
  and and_11 (and_11_out, and_1_out, xor_1_out);
  and and_12 (and_12_out, xor_1_out, and_4_out, xor_2_out);
  and and_13 (and_13_out, xor_1_out, xor_2_out, and_3_out, xor_3_out, c0);
  and and_14 (and_14_out, xor_1_out, xor_2_out, xor_4_out, and_3_out);
  or c3 (c3_out, and_8_out, and_9_out, and_10_out, and_1_out);
  xor xor_5 (s0, c0, xor_3_out);
  xor xor_6 (s1, c1_out, xor_4_out);
  xor xor_7 (s2, c2_out, xor_2_out);
  xor xor_8 (s3, c3_out, and_11_out);
  or c4 (out_9, and_11_out, and_12_out, and_13_out, and_14_out, and_2_out);
  Hex_Digit_Display hex_digit_display_1 (.value({s3, s2, s1, s0}));  // open: dp
endmodule
